// Digital circuit alu.dig as structural Verilog
module alu (
  input  [7:0] a_in,
  input  [7:0] b_in,
  input  ena,
  input  sub,
  output [7:0] peek,
  output c_o,
  output [7:0] bus_out
);

  Add #(.Bits(8)) add_1 (.a(a_in), .b(b_in), .c_i(1'b0), .s(peek), .c_o(c_o));
  assign bus_out = ena ? peek : 8'bz;  // Driver driver_1
  // also tied to GND on the sheet: sub
endmodule
