// Digital circuit alu_v2.dig as structural Verilog
module alu_v2 (
  input  [7:0] a_in,
  input  [7:0] b_in,
  input  clk,
  input  [2:0] OPSEL,
  input  rset,
  input  fi,
  input  fc,
  input  fo,
  input  [7:0] bus_in,
  input  [7:0] x_in,
  input  a_d,
  input  [2:0] x_d,
  output [7:0] flags_peek,
  output [7:0] bus_out
);

  wire alu_d, carry, comparator_1_eq, comparator_1_gt, comparator_1_lt, opsel_add, opsel_and, opsel_cmp,
       opsel_or, opsel_sl, opsel_sr, opsel_xor, or_9_out, or_10_out, or_13_out, or_14_out, x_d_t;
  wire [1:0] add_1_c_o, driver_4_out;
  wire [1:1] nor_1_out, nor_2_out, nor_3_out;
  wire [2:2] lookuptable_1_out_2;
  wire [3:0] lookuptable_2_out;
  wire [7:0] a_d_flags, add_1_s, alu_d_flags, and_1_out, and_2_out, and_3_out, and_4_out, and_5_out,
       and_6_out, and_7_out, driver_13_out, lookuptable_1_out, or_3_out, or_5_out, or_8_out, or_11_out,
       or_12_out, x_d_flags, xor_1_out;

  Decoder #(.Selector_Bits(3)) decoder_1 (
    .sel(OPSEL), .out_1(opsel_add), .out_2(opsel_and), .out_3(opsel_or), .out_4(opsel_xor), .out_5(opsel_sl),
    .out_6(opsel_sr), .out_7(opsel_cmp));  // open: out_0
  or or_1 (x_d_t, x_d[0], x_d[1], x_d[2]);
  or or_2 (alu_d, OPSEL[0], OPSEL[1], OPSEL[2]);
  nor nor_1 (nor_1_out[1], bus_in[0], bus_in[1], bus_in[2], bus_in[3], bus_in[4], bus_in[5], bus_in[6], bus_in[7]);
  Add #(.Bits(8)) add_1 (.a(a_in), .b(b_in), .c_i(carry), .s(add_1_s), .c_o(add_1_c_o[0]));
  Comparator #(.Bits(8)) comparator_1 (
    .a(a_in), .b(b_in), .gt(comparator_1_gt), .eq(comparator_1_eq), .lt(comparator_1_lt));
  assign and_1_out = a_in & b_in;  // And and_1, 8 bits wide
  assign or_3_out = a_in | b_in;  // Or or_3, 8 bits wide
  assign xor_1_out = a_in ^ b_in;  // XOr xor_1, 8 bits wide
  assign and_2_out = 8'h7d & flags_peek;  // And and_2, 8 bits wide
  assign a_d_flags = and_2_out | {bus_in[7], {5{1'b0}}, nor_1_out[1], 1'b0};  // Or or_4, 8 bits wide
  assign bus_out = opsel_and ? and_1_out : 8'bz;  // Driver driver_1
  assign bus_out = opsel_or ? or_3_out : 8'bz;  // Driver driver_2
  assign bus_out = opsel_xor ? xor_1_out : 8'bz;  // Driver driver_3
  assign driver_4_out[0] = opsel_sl ? a_in[7] : 1'bz;  // Driver driver_4
  assign bus_out = opsel_sl ? {a_in[6:0], carry} : 8'bz;  // Driver driver_5
  assign driver_4_out[0] = opsel_sr ? a_in[0] : 1'bz;  // Driver driver_6
  assign bus_out = opsel_sr ? {carry, a_in[7:1]} : 8'bz;  // Driver driver_7
  LookUpTable #(.Bits(3)) lookuptable_1 (
    .in0(comparator_1_gt), .in1(comparator_1_eq), .in2(comparator_1_lt),
    .out({lookuptable_1_out_2[2], lookuptable_1_out[1:0]}));
  nor nor_2 (nor_2_out[1], bus_out[0], bus_out[1], bus_out[2], bus_out[3], bus_out[4], bus_out[5], bus_out[6], bus_out[7]);
  nor nor_3 (nor_3_out[1], bus_in[0], bus_in[1], bus_in[2], bus_in[3], bus_in[4], bus_in[5], bus_in[6], bus_in[7]);
  assign and_3_out = 8'h7d & flags_peek;  // And and_3, 8 bits wide
  assign and_4_out = 8'h7d & flags_peek;  // And and_4, 8 bits wide
  assign bus_out = opsel_add ? add_1_s : 8'bz;  // Driver driver_8
  nor nor_4 (driver_4_out[1], bus_out[0], bus_out[1], bus_out[2], bus_out[3], bus_out[4], bus_out[5], bus_out[6], bus_out[7]);
  assign or_5_out = and_3_out | {bus_out[7], {5{1'b0}}, nor_2_out[1], 1'b0};  // Or or_5, 8 bits wide
  assign x_d_flags = and_4_out | {bus_in[7], {5{1'b0}}, nor_3_out[1], 1'b0};  // Or or_6, 8 bits wide
  Comparator #(.Bits(8)) comparator_2 (.a(add_1_s), .b({8{1'b0}}), .eq(add_1_c_o[1]));  // open: gt, lt
  assign and_5_out = flags_peek & 8'h7c;  // And and_5, 8 bits wide
  or or_7 (lookuptable_1_out[7], lookuptable_1_out_2[2], a_in[7]);
  assign and_6_out = 8'h7c & flags_peek;  // And and_6, 8 bits wide
  assign or_8_out = and_6_out | {bus_out[7], {5{1'b0}}, driver_4_out};  // Or or_8, 8 bits wide
  assign alu_d_flags = or_9_out ? or_5_out : 8'bz;  // Driver driver_9
  or or_9 (or_9_out, opsel_and, opsel_or, opsel_xor);
  assign and_7_out = flags_peek & 8'hfc;  // And and_7, 8 bits wide
  assign alu_d_flags = or_10_out ? or_8_out : 8'bz;  // Driver driver_10
  or or_10 (or_10_out, opsel_sr, opsel_sl);
  assign or_11_out = and_7_out | {{6{1'b0}}, add_1_c_o};  // Or or_11, 8 bits wide
  assign or_12_out = and_5_out | {lookuptable_1_out[7], {5{1'b0}}, lookuptable_1_out[1:0]};  // Or or_12, 8 bits wide
  assign alu_d_flags = opsel_cmp ? or_12_out : 8'bz;  // Driver driver_11
  assign alu_d_flags = opsel_add ? or_11_out : 8'bz;  // Driver driver_12
  or or_13 (or_13_out, a_d, x_d_t, fi, alu_d);
  LookUpTable #(.Bits(4)) lookuptable_2 (.in0(fi), .in1(alu_d), .in2(a_d), .in3(x_d_t), .out(lookuptable_2_out));
  // Probe reg_set on or_13_out
  assign driver_13_out = lookuptable_2_out[3] ? x_d_flags : 8'bz;  // Driver driver_13
  assign driver_13_out = lookuptable_2_out[2] ? a_d_flags : 8'bz;  // Driver driver_14
  or or_14 (or_14_out, fc, rset);
  assign driver_13_out = lookuptable_2_out[1] ? alu_d_flags : 8'bz;  // Driver driver_15
  assign driver_13_out = lookuptable_2_out[0] ? bus_in : 8'bz;  // Driver driver_16
  register FLAGS (
    .bus_in(driver_13_out), .clk(clk), .rfb(or_13_out), .wtb(fo), .rset(or_14_out), .inc(1'b0),
    .bus_out(bus_out), .peek(flags_peek));  // open: cry
  // Probe reg_in on driver_13_out
  D_FF d_ff_1 (.D(flags_peek[0]), .C(clk), .Q(carry));  // open: nQ

  // Notes on the sheet:
  //   Compare Instruction Results
  //   Compare Result	N	Z	C
  //   A, X, or Y < Memory	*	0	0      0b*0000000
  //   A, X, or Y = Memory	0	1	1      0b00000011
  //   A, X, or Y > Memory	*	0	1      0b*0000001
  //   * The N flag will be bit 7 of A, X, or Y - Memory
  //   Flags Register BIts
  //   Carry
  //   Equal/Zero (one flag)
  //   Overflow
  //   negative
  //   7  bit  0
  //   ---- ----
  //   NV1B DIZC
  //   |||| ||||
  //   |||| |||+- Carry
  //   |||| ||+-- Zero
  //   |||| |+--- Interrupt Disable
  //   |||| +---- Decimal
  //   |||+------ (No CPU effect; see: the B flag)
  //   ||+------- (No CPU effect; always pushed as 1)
  //   |+-------- Overflow
  //   +--------- Negative
  //   Shift
  //   Left
  //   Shift
  //   Right
  //   contents of lookuptable_1 (hex, n*v repeats v):
  //   0,1,3
  //   res->NZ
  //   TODO: all ALU ops can go
  //   through these two
  //   flags-setters
  //   res->NZC
  //   contents of lookuptable_2 (hex, n*v repeats v):
  //   0,1,2,1,4,1,2,1,8,1,2,1,4,1,2,1
  //   Addition & Subtraction
  //   FLAGS:
  //   Set overflow if overflow during sub, which is if carry bit is set
  //   Set carry flag if carry is set on addition
  //   FIXME: Carry from current op fed back in and affects result of current op!
endmodule

/* Test case add sub:
clk fc OPSEL a_in b_in flags_peek bus_out
# NV1B DIZC
# Addition Tests
C 0 1 0x00 0xff 0b00000000 0xff
C 0 1 0xff 0x01 0b00000011 0x00
# Clear Carry - not sure why requires 2 ticks!
C 1 0 0x00 0x00 X          X
C 0 0 0x00 0x00 X          X
C 0 1 0xff 0x00 0b00000000 0xff
#C 0 1 0x80 0x00 0b10000000 0x80

# Subtraction Tests
#C 0 2 0x04 0x01 0b00000000 0x03
#C 0 2 0x04 0x04 0b00000010 0x00
#C 0 2 0x04 0x06 0b10000001 0xFE

# Clear test
C 1 0 0x00 0x00 X Z
# NO-OP test
C 0 0 0x12 0x34 0b00000000 Z
*/

/* Test case flags set logic:
clk fc fi OPSEL a_d x_d  bus_in a_in b_in  x_in    reg_set reg_in bus_out
# Test when nothing is set                                        
C   0  0  0     0   0    0xff   0x001 0x02 0x03    0       Z      X

# Test write to flags from bus
C   0  1  0     0   0    0xff   0x001 0x02 0x03    1       0xff   X
C   0  1  1     1   0    0xff   0x001 0x02 0x03    1       0xff   X
C   0  1  0     0   1    0xff   0x001 0x02 0x03    1       0xff   X

# Clear reg for next test
C   1  0  0     0   0    0xff   0x001 0x02 0x03    0       Z      X
C   1  0  0     0   0    0xff   0x001 0x02 0x03    0       Z      X
# Test Math Op
C   0  0  1     0   0    0xff   0x01 0xff 0x03     1       0x03   X
C   0  0  1     0   0    0xff   0x01 0xf0 0x03     1       0x00   X

# Clear reg for next test
C   1  0  0     0   0    0xff   0x001 0x02 0x03    0       Z      X
# Test accum Op
C   0  0  0     1   0    0xff   0x00 0x02 0x03    1       0x02    X
C   0  0  0     1   1    0xff   0x00 0x02 0x03    1       0x02    X

# Clear reg for next test
C   1  0  0     0   0    0xff   0x001 0x02 0x03    0       Z      X
# test X Op
C   0  0  0     0   1    0xff   0x00 0x02 0xff    1       0x80    X
C   0  0  0     0   1    0xff   0x00 0x02 0xff    1       0x80    X
*/

/* Test case Compare:
clk OPSEL a_in b_in flags_peek
# A < B ; A = B ; A > B
C 7 0x00 0xff 0b00000000
C 7 0x02 0x02 0b00000011
C 7 0x0f 0x00 0b00000001

# Tests with negative results
C 7 0x81 0x83 0b10000000
# NOTE - not sure negative flag behavior,
# right now its just based on A?
C 7 0x81 0x81 0b10000011
# THIS TEST IS NOT WORKING
# C 7 0x8D 0x8F 0b10000011
C 7 0x8D 0x8F X
*/

/* Test case shifts:
clk fc fi OPSEL a_in        reg_set  reg_in     bus_out
# Test when nothing is set
C   0  0  0     0b000000000  0       Z          Z
C   1  0  0     0x000000000  0       Z          X

# Test shift left 0x05
C   0  0  0x05   0b00000001  1       0b00000000 0b00000010
C   0  0  0x05   0b10000000  1       0b00000011 0b00000000
C   0  0  0x05   0b00000000  1       0b00000000 0b00000001

# test shift right 0x06
C   0  0  0x06   0b00000010  1       0b00000000 0b00000001
C   0  0  0x06   0b00000001  1       0b00000011 0b00000000
C   0  0  0x06   0b00000000  1       0b10000000 0b10000000
*/

/* Test case logic ops:
clk fc fi OPSEL a_in b_in reg_set reg_in     bus_out
# Test when nothing is set
C   0  0  0     0x00 0x00 0       Z          X
C   1  0  0     0x00 0x00 0       Z          X
#
# And 0x02
C   0  0  0x02  0x00 0x00 1       0b00000010 0x00
C   0  0  0x02  0x02 0x02 1       0b00000000 0x02

# Or 0x03
C   0  0  0x02  0x00 0x04 1       0b00000010 0x00
C   0  0  0x03  0x02 0x01 1       0b00000000 0x03

# Xor 0x04
C   0  0  0x04  0x00 0x04 1       0b00000000 0x04
C   0  0  0x04  0x03 0x01 1       0b00000000 0x02
*/
