// Digital circuit alu_v3.dig as structural Verilog
module alu_v3 (
  input  [7:0] a_in,
  input  [7:0] b_in,
  input  clk,
  input  [2:0] OPSEL,
  input  rset,
  input  fi,
  input  fc,
  input  fo,
  input  [7:0] bus_in,
  input  [7:0] x_in,
  input  a_din,
  input  [2:0] x_din,
  output [7:0] flags_peek,
  output [7:0] bus_out
);

  wire alu_d, carry, comparator_1_eq, comparator_1_gt, comparator_1_lt, opsel_add, opsel_and, opsel_cmp,
       opsel_or, opsel_sl, opsel_sr, opsel_xor, or_11_out, or_12_out, x_d;
  wire [1:0] add_1_c_o, dflagslut_out, logiclut_out, multiplexer_1_out;
  wire [1:1] nor_1_out, nor_2_out;
  wire [2:2] cmplut_out_2;
  wire [6:0] multiplexer_2_out;
  wire [7:0] a_d_flags, add_d_flags, alu_d_flags, alu_out, and_2_out, and_3_out, and_4_out, and_5_out,
       and_6_out, and_7_out, cmp_d_flags, cmplut_out, FLAGS_p8, logic_d_flags, multiplexer_3_out,
       multiplexer_4_out, res_add, res_and, res_or, res_xor, shift_d_flags, x_d_flags;
  wire [7:1] multiplexer_2_out_2;

  Decoder #(.Selector_Bits(3)) decoder_1 (
    .sel(OPSEL), .out_1(opsel_add), .out_2(opsel_and), .out_3(opsel_or), .out_4(opsel_xor), .out_5(opsel_sl),
    .out_6(opsel_sr), .out_7(opsel_cmp));  // open: out_0
  or or_1 (x_d, x_din[0], x_din[1], x_din[2]);
  or or_2 (alu_d, OPSEL[0], OPSEL[1], OPSEL[2]);
  nor nor_1 (nor_1_out[1], bus_in[0], bus_in[1], bus_in[2], bus_in[3], bus_in[4], bus_in[5], bus_in[6], bus_in[7]);
  Add #(.Bits(8)) add_1 (.a(a_in), .b(b_in), .c_i(carry), .s(res_add), .c_o(add_1_c_o[0]));
  Comparator #(.Bits(8)) comparator_1 (
    .a(a_in), .b(b_in), .gt(comparator_1_gt), .eq(comparator_1_eq), .lt(comparator_1_lt));
  assign res_and = a_in & b_in;  // And and_1, 8 bits wide
  assign res_or = a_in | b_in;  // Or or_3, 8 bits wide
  assign res_xor = a_in ^ b_in;  // XOr xor_1, 8 bits wide
  assign and_2_out = 8'h7d & flags_peek;  // And and_2, 8 bits wide
  assign a_d_flags = and_2_out | {bus_in[7], {5{1'b0}}, nor_1_out[1], 1'b0};  // Or or_4, 8 bits wide
  LookUpTable #(.Bits(2)) logiclut (.in0(opsel_and), .in1(opsel_or), .in2(opsel_xor), .out(logiclut_out));
  Multiplexer multiplexer_1 (.sel(opsel_sr), .in_0(a_in[7]), .in_1(a_in[0]), .out(multiplexer_1_out[0]));
  Multiplexer #(.Selector_Bits(2), .Bits(8)) multiplexer_2 (
    .sel(logiclut_out), .in_0(res_and), .in_1(res_or), .in_2(res_xor), .in_3({8{1'b0}}),
    .out({multiplexer_2_out_2[7], multiplexer_2_out}));
  LookUpTable #(.Bits(3)) cmplut (
    .in0(comparator_1_gt), .in1(comparator_1_eq), .in2(comparator_1_lt),
    .out({cmplut_out_2[2], cmplut_out[1:0]}));
  Multiplexer #(.Bits(8)) multiplexer_3 (
    .sel(opsel_sr), .in_0({a_in[6:0], carry}), .in_1({carry, a_in[7:1]}), .out(multiplexer_3_out));
  nor nor_2 (nor_2_out[1], bus_in[0], bus_in[1], bus_in[2], bus_in[3], bus_in[4], bus_in[5], bus_in[6], bus_in[7]);
  assign and_3_out = 8'h7d & flags_peek;  // And and_3, 8 bits wide
  nor nor_3 (multiplexer_1_out[1], multiplexer_3_out[0], multiplexer_3_out[1], multiplexer_3_out[2], multiplexer_3_out[3], multiplexer_3_out[4], multiplexer_3_out[5], multiplexer_3_out[6], multiplexer_3_out[7]);
  assign x_d_flags = and_3_out | {bus_in[7], {5{1'b0}}, nor_2_out[1], 1'b0};  // Or or_5, 8 bits wide
  Comparator #(.Bits(8)) comparator_2 (.a(res_add), .b({8{1'b0}}), .eq(add_1_c_o[1]));  // open: gt, lt
  assign and_4_out = flags_peek & 8'h7c;  // And and_4, 8 bits wide
  or or_6 (cmplut_out[7], cmplut_out_2[2], a_in[7]);
  assign and_5_out = 8'h7c & flags_peek;  // And and_5, 8 bits wide
  assign shift_d_flags = and_5_out | {multiplexer_3_out[7], {5{1'b0}}, multiplexer_1_out};  // Or or_7, 8 bits wide
  nor nor_4 (multiplexer_2_out_2[1], multiplexer_2_out[0], multiplexer_2_out[1], multiplexer_2_out[2], multiplexer_2_out[3], multiplexer_2_out[4], multiplexer_2_out[5], multiplexer_2_out[6], multiplexer_2_out_2[7]);
  assign and_6_out = flags_peek & 8'hfc;  // And and_6, 8 bits wide
  assign and_7_out = 8'h7d & flags_peek;  // And and_7, 8 bits wide
  assign logic_d_flags = and_7_out | {multiplexer_2_out_2[7], {5{1'b0}}, multiplexer_2_out_2[1], 1'b0};  // Or or_8, 8 bits wide
  assign add_d_flags = and_6_out | {{6{1'b0}}, add_1_c_o};  // Or or_9, 8 bits wide
  assign cmp_d_flags = and_4_out | {cmplut_out[7], {5{1'b0}}, cmplut_out[1:0]};  // Or or_10, 8 bits wide
  or or_11 (or_11_out, a_din, x_d, fi, alu_d);
  LookUpTable #(.Bits(2)) dflagslut (.in0(fi), .in1(alu_d), .in2(a_din), .in3(x_d), .out(dflagslut_out));
  // Probe reg_set on or_11_out
  Multiplexer #(.Selector_Bits(2), .Bits(8)) multiplexer_4 (
    .sel(dflagslut_out), .in_0(x_d_flags), .in_1(bus_in), .in_2(alu_d_flags), .in_3(a_d_flags),
    .out(multiplexer_4_out));
  or or_12 (or_12_out, fc, rset);
  // Probe reg_in on multiplexer_4_out
  // register FLAGS: pin names not known; wires that end beside it: multiplexer_4_out, clk, or_11_out, fo, or_12_out, 1'b0, 1'b0, FLAGS_p8, flags_peek
  Multiplexer #(.Selector_Bits(3), .Bits(8)) multiplexer_5 (
    .sel(OPSEL), .in_0({8{1'b0}}), .in_1(add_d_flags), .in_2(logic_d_flags), .in_3(logic_d_flags),
    .in_4(logic_d_flags), .in_5(shift_d_flags), .in_6(shift_d_flags), .in_7(cmp_d_flags), .out(alu_d_flags));
  Multiplexer #(.Selector_Bits(3), .Bits(8)) multiplexer_6 (
    .sel(OPSEL), .in_0({8{1'b0}}), .in_1(res_add), .in_2(res_and), .in_3(res_or), .in_4(res_xor),
    .in_5({a_in[6:0], carry}), .in_6({carry, a_in[7:1]}), .in_7({8{1'b0}}), .out(alu_out));
  Multiplexer #(.Bits(8)) multiplexer_7 (.sel(fo), .in_0(alu_out), .in_1(FLAGS_p8), .out(bus_out));
  D_FF d_ff_1 (.D(flags_peek[0]), .C(clk), .Q(carry));  // open: nQ

  // Other names for the same wires on the sheet: a_d = a_din; res_sl[7:0] = {a_in[6:0], carry};
  //   res_sr[7:0] = {carry, a_in[7:1]}

  // Notes on the sheet:
  //   Compare Instruction Results
  //   Compare Result	N	Z	C
  //   A, X, or Y < Memory	*	0	0      0b*0000000
  //   A, X, or Y = Memory	0	1	1      0b00000011
  //   A, X, or Y > Memory	*	0	1      0b*0000001
  //   * The N flag will be bit 7 of A, X, or Y - Memory
  //   Flags Register BIts
  //   Carry
  //   Equal/Zero (one flag)
  //   Overflow
  //   negative
  //   7  bit  0
  //   ---- ----
  //   NV1B DIZC
  //   |||| ||||
  //   |||| |||+- Carry
  //   |||| ||+-- Zero
  //   |||| |+--- Interrupt Disable
  //   |||| +---- Decimal
  //   |||+------ (No CPU effect; see: the B flag)
  //   ||+------- (No CPU effect; always pushed as 1)
  //   |+-------- Overflow
  //   +--------- Negative
  //   Shift
  //   Left
  //   Shift
  //   Right
  //   contents of logiclut (hex, n*v repeats v):
  //   0,0,15,0,2
  //   contents of cmplut (hex, n*v repeats v):
  //   0,1,3
  //   TODO: all ALU ops can go
  //   through these two
  //   flags-setters
  //   res->NZC
  //   res->NZ
  //   contents of dflagslut (hex, n*v repeats v):
  //   0,1,2,1,3,1,2,1,4,1,2,1,3,1,2,1
  //   Addition & Subtraction
  //   FLAGS:
  //   Set overflow if overflow during sub, which is if carry bit is set
  //   Set carry flag if carry is set on addition
  //   FIXME: Carry from current op fed back in and affects result of current op!
endmodule

/* Test case add sub:
clk fc OPSEL a_in b_in flags_peek bus_out
# NV1B DIZC
# Addition Tests
C 0 1 0x00 0xff 0b00000000 0xff
C 0 1 0xff 0x01 0b00000011 0x00
# Clear Carry - not sure why requires 2 ticks!
C 1 0 0x00 0x00 X          X
C 0 0 0x00 0x00 X          X
C 0 1 0xff 0x00 0b00000000 0xff
#C 0 1 0x80 0x00 0b10000000 0x80

# Subtraction Tests
#C 0 2 0x04 0x01 0b00000000 0x03
#C 0 2 0x04 0x04 0b00000010 0x00
#C 0 2 0x04 0x06 0b10000001 0xFE

# Clear test
C 1 0 0x00 0x00 X X
# NO-OP test
C 0 0 0x12 0x34 0b00000000 X
*/

/* Test case flags set logic:
clk fc fi OPSEL a_d x_d  bus_in a_in b_in  x_in    reg_set reg_in bus_out
# Test when nothing is set                                        
C   0  0  0     0   0    0xff   0x001 0x02 0x03    0       X      X

# Test write to flags from bus
C   0  1  0     0   0    0xff   0x001 0x02 0x03    1       0xff   X
C   0  1  1     1   0    0xff   0x001 0x02 0x03    1       0xff   X
C   0  1  0     0   1    0xff   0x001 0x02 0x03    1       0xff   X

# Clear reg for next test
C   1  0  0     0   0    0xff   0x001 0x02 0x03    0       X      X
C   1  0  0     0   0    0xff   0x001 0x02 0x03    0       X      X
# Test Math Op
C   0  0  1     0   0    0xff   0x01 0xff 0x03     1       0x03   X
C   0  0  1     0   0    0xff   0x01 0xf0 0x03     1       0x00   X

# Clear reg for next test
C   1  0  0     0   0    0xff   0x001 0x02 0x03    0       X      X
# Test accum Op
# BUG expected: zero flag, actual: negative flag
C   0  0  0     1   0    0xff   0x00 0x02 0x03    1       0x02    X
C   0  0  0     1   1    0xff   0x00 0x02 0x03    1       0x02    X

# Clear reg for next test
C   1  0  0     0   0    0xff   0x001 0x02 0x03    0       X      X
# test X Op
C   0  0  0     0   1    0xff   0x00 0x02 0xff    1       0x80    X
C   0  0  0     0   1    0xff   0x00 0x02 0xff    1       0x80    X
*/

/* Test case Compare:
clk OPSEL a_in b_in flags_peek
# A < B ; A = B ; A > B
C 7 0x00 0xff 0b00000000
C 7 0x02 0x02 0b00000011
C 7 0x0f 0x00 0b00000001

# Tests with negative results
C 7 0x81 0x83 0b10000000
# NOTE - not sure negative flag behavior,
# right now its just based on A?
C 7 0x81 0x81 0b10000011
# THIS TEST IS NOT WORKING
# C 7 0x8D 0x8F 0b10000011
C 7 0x8D 0x8F X
*/

/* Test case shifts:
clk fc fi OPSEL a_in        reg_set  reg_in     bus_out
# Test when nothing is set
C   0  0  0     0b000000000  0       X          X
C   1  0  0     0x000000000  0       X          X

# Test shift left 0x05
C   0  0  0x05   0b00000001  1       0b00000000 0b00000010
C   0  0  0x05   0b10000000  1       0b00000011 0b00000000
C   0  0  0x05   0b00000000  1       0b00000000 0b00000001

# test shift right 0x06
C   0  0  0x06   0b00000010  1       0b00000000 0b00000001
C   0  0  0x06   0b00000001  1       0b00000011 0b00000000
C   0  0  0x06   0b00000000  1       0b10000000 0b10000000
*/

/* Test case logic ops:
clk fc fi OPSEL a_in b_in reg_set reg_in     bus_out
# Test when nothing is set
C   0  0  0     0x00 0x00 0       X          X
C   1  0  0     0x00 0x00 0       X          X
#
# And 0x02
C   0  0  0x02  0x00 0x00 1       0b00000010 0x00
C   0  0  0x02  0x02 0x02 1       0b00000000 0x02

# Or 0x03
C   0  0  0x02  0x00 0x04 1       0b00000010 0x00
C   0  0  0x03  0x02 0x01 1       0b00000000 0x03

# Xor 0x04
C   0  0  0x04  0x00 0x04 1       0b00000000 0x04
C   0  0  0x04  0x03 0x01 1       0b00000000 0x02
*/
