// Digital circuit computer.dig as structural Verilog
module computer (
  input  clk,
  output [15:0] addrbus,
  output out_3
);

  wire ai, als1, als2, als3, and_1_out, and_3_out, and_4_out, ao, bi, bo, ci, clk_t, decoder_1_out_0,
       decoder_1_out_1, decoder_1_out_2, decoder_1_out_3, hlt, Man_Auto_out, not_1_out, not_2_out, or_1_out,
       rset, t_ff_1_q, Tick_out;
  wire [3:0] irc_peek;
  wire [7:0] acc_peek, cpu_1_dbus_out, dbus, fr_peek, IO_sd, ir_peek, m_dbus;
  wire [31:0] cont_peek;

  cpu cpu_1 (
    .rset(rset), .dbus_in(dbus), .clk(clk_t), .abus_out(addrbus), .dbus_out(cpu_1_dbus_out),
    .cont_peek({cont_peek[31:18], als3, als2, als1, bo, bi, cont_peek[12:5], ao, ai, cont_peek[2], ci, cont_peek[0]}),
    .irc_peek(irc_peek), .ir_peek(ir_peek), .acc_peek(acc_peek), .hlt(hlt), .fr_peek(fr_peek));
  T_FF t_ff_1 (.T(Man_Auto_out), .C(Man_Auto_out), .Q(t_ff_1_q), .nQ(out_3));
  Button Man_Auto (.out(Man_Auto_out));
  Reset reset_1 ();  // open: out
  Seven_Seg_Hex seven_seg_hex_1 (.d(ir_peek[7:4]), .dp(1'b0));
  Button Tick (.out(Tick_out));
  and and_1 (and_1_out, t_ff_1_q, clk);
  not not_1 (not_1_out, hlt);
  Button button_1 (.out(rset));
  LED led_1 (.in(acc_peek[0]));
  LED led_2 (.in(acc_peek[2]));
  LED led_3 (.in(acc_peek[1]));
  LED led_4 (.in(dbus[0]));
  LED led_5 (.in(dbus[2]));
  LED led_6 (.in(dbus[1]));
  Seven_Seg_Hex seven_seg_hex_2 (.d(ir_peek[3:0]), .dp(1'b1));
  and and_2 (clk_t, or_1_out, not_1_out);
  LED led_7 (.in(acc_peek[4]));
  LED led_8 (.in(acc_peek[6]));
  LED led_9 (.in(acc_peek[3]));
  LED led_10 (.in(acc_peek[5]));
  LED led_11 (.in(dbus[4]));
  LED led_12 (.in(dbus[6]));
  LED led_13 (.in(dbus[3]));
  LED led_14 (.in(dbus[5]));
  Multiplexer #(.Bits(8)) multiplexer_1 (.sel(cont_peek[11]), .in_0(cpu_1_dbus_out), .in_1(m_dbus), .out(dbus));
  Seven_Seg_Hex seven_seg_hex_3 (.d(irc_peek), .dp(1'b0));
  or or_1 (or_1_out, Tick_out, and_1_out);
  LED led_15 (.in(acc_peek[7]));
  LED led_16 (.in(dbus[7]));
  LED led_17 (.in(cont_peek[0]));
  LED led_18 (.in(cont_peek[2]));
  LED led_19 (.in(ci));
  Decoder #(.Selector_Bits(2)) decoder_1 (
    .sel(addrbus[15:14]), .out_0(decoder_1_out_0), .out_1(decoder_1_out_1), .out_2(decoder_1_out_2),
    .out_3(decoder_1_out_3));
  LED led_20 (.in(ao));
  LED led_21 (.in(cont_peek[6]));
  LED led_22 (.in(ai));
  LED led_23 (.in(cont_peek[5]));
  LED led_24 (.in(cont_peek[8]));
  LED led_25 (.in(cont_peek[10]));
  LED led_26 (.in(cont_peek[7]));
  LED led_27 (.in(cont_peek[9]));
  and and_3 (and_3_out, cont_peek[12], decoder_1_out_0);
  and and_4 (and_4_out, decoder_1_out_2, cont_peek[12]);
  LED led_28 (.in(cont_peek[12]));
  LED led_29 (.in(bo));
  LED led_30 (.in(cont_peek[11]));
  LED led_31 (.in(bi));
  ROM #(.AddrBits(14), .Bits(8)) System_ROM (.A(addrbus[13:0]), .sel(decoder_1_out_3), .D(m_dbus));
  LED led_32 (.in(cont_peek[18]));
  LED led_33 (.in(als2));
  LED led_34 (.in(als1));
  LED led_35 (.in(als3));
  RAMDualPort #(.AddrBits(14), .Bits(8)) lowermem (
    .A(addrbus[13:0]), .Din(dbus), .str(and_3_out), .C(clk_t), .ld(decoder_1_out_0), .D(m_dbus));
  mmio_v2 IO (
    .bus_in(dbus), .rfb(and_4_out), .clk(clk_t), .wtb(decoder_1_out_2), .rset(rset), .addr_in(addrbus[5:0]),
    .addr_set({6{1'b0}}), .bus_out(m_dbus), .sd(IO_sd));
  LED led_36 (.in(cont_peek[20]));
  LED led_37 (.in(cont_peek[22]));
  LED led_38 (.in(cont_peek[19]));
  LED led_39 (.in(cont_peek[21]));
  LED led_40 (.in(cont_peek[24]));
  LED led_41 (.in(cont_peek[26]));
  LED led_42 (.in(cont_peek[23]));
  LED led_43 (.in(cont_peek[25]));
  LED led_44 (.in(IO_sd[0]));
  LED led_45 (.in(IO_sd[2]));
  LED led_46 (.in(IO_sd[1]));
  LED led_47 (.in(IO_sd[3]));
  Seven_Seg_Hex seven_seg_hex_4 (.d(IO_sd[7:4]), .dp(1'b0));
  LED led_48 (.in(cont_peek[28]));
  LED led_49 (.in(cont_peek[30]));
  LED led_50 (.in(cont_peek[27]));
  LED led_51 (.in(cont_peek[29]));
  LED led_52 (.in(IO_sd[4]));
  LED led_53 (.in(IO_sd[6]));
  LED led_54 (.in(IO_sd[5]));
  LED led_55 (.in(IO_sd[7]));
  Seven_Seg_Hex seven_seg_hex_5 (.d(IO_sd[3:0]), .dp(1'b0));
  LED led_56 (.in(cont_peek[31]));
  not not_2 (not_2_out, hlt);
  // fpga_leds fpga_leds_1: pin names not known; wires that end beside it: fr_peek[1], not_2_out, IO_sd

  // Other names for the same wires on the sheet: abus[15:0] = addrbus; abus_out[15:0] = addrbus; minc = cont_peek[0];
  //   cont_peek (some bits) = {als3, als2, als1, bo, bi, ao, ai, ci}; xi = cont_peek[2]; mrli = cont_peek[5];
  //   xo = cont_peek[6]; end = cont_peek[7]; ms1 = cont_peek[8]; ms2 = cont_peek[9]; iri = cont_peek[10];
  //   mo = cont_peek[11]; mi = cont_peek[12]; pcc1 = cont_peek[18]; pcc2 = cont_peek[19]; pcc3 = cont_peek[20];
  //   fi = cont_peek[21]; fc = cont_peek[22]; fo = cont_peek[23]; mrhi = cont_peek[24]; pclo = cont_peek[25];
  //   pcho = cont_peek[26]; spu = cont_peek[27]; spd = cont_peek[28]; spo = cont_peek[29]; xu = cont_peek[30];
  //   xd = cont_peek[31]

  // Notes on the sheet:
  //   clk: Hz: 50
  //   addrbus: The Address Bus
  //   Bank Sel
  //   Future Video Memory
  //   0x4000-0x7FFF
  //   IO Space 0x8000 - 0xBFFF
  //   contents of System_ROM (hex, n*v repeats v):
  //   127*0,10
  //   ROM 0xC000 - 0xFFFF
endmodule
