// Digital circuit cpu.dig as structural Verilog
module cpu (
  input  rset,
  input  [7:0] dbus_in,
  input  clk,
  output [15:0] abus_out,
  output [7:0] dbus_out,
  output [31:0] cont_peek,
  output [3:0] irc_peek,
  output [7:0] ir_peek,
  output [7:0] acc_peek,
  output hlt,
  output [7:0] fr_peek
);

  wire MRH_p6, MRH_p9, MRL_p9, or_1_out, PC_CONT_pchi, PC_CONT_pcli, PCH_p6;
  wire [3:0] priorityencoder_1_num;
  wire [7:0] a_dbus, alu_dbus, b_dbus, f_dbus, MRH_p8, MRL_p8, PC_CONT_pch_bo, PC_CONT_pcl_bo, pch_dbus,
       pcl_dbus, REG_B_p10, sp_dbus, SP_p9, x_dbus, x_peek;
  wire [15:0] pca;

  or or_1 (or_1_out, cont_peek[15], cont_peek[16], cont_peek[17]);
  Multiplexer #(.Selector_Bits(4), .Bits(8)) multiplexer_1 (
    .sel(priorityencoder_1_num), .in_0(x_dbus), .in_1(b_dbus), .in_2(a_dbus), .in_3(f_dbus), .in_4(pcl_dbus),
    .in_5(pch_dbus), .in_6(sp_dbus), .in_7(dbus_in), .in_8(alu_dbus), .in_9({8{1'b0}}), .in_10({8{1'b0}}),
    .in_11({8{1'b0}}), .in_12({8{1'b0}}), .in_13({8{1'b0}}), .in_14({8{1'b0}}), .in_15({8{1'b0}}),
    .out(dbus_out));
  PriorityEncoder #(.Selector_Bits(4)) priorityencoder_1 (
    .in0(cont_peek[6]), .in1(cont_peek[14]), .in2(cont_peek[4]), .in3(cont_peek[23]), .in4(cont_peek[25]),
    .in5(cont_peek[26]), .in6(cont_peek[29]), .in7(cont_peek[11]), .in8(or_1_out), .in9(1'b0), .in10(1'b0),
    .in11(1'b0), .in12(1'b0), .in13(1'b0), .in14(1'b0), .in15(1'b0), .num(priorityencoder_1_num));  // open: any
  Counter #(.Bits(4)) irc (.en(1'b1), .C(clk), .clr(cont_peek[7]), .out(irc_peek));  // open: ovf
  // register IR: pin names not known; wires that end beside it: dbus_out, clk, cont_peek[10], 1'b0, rset, 1'b0, 1'b0, ir_peek
  // register REG_A: pin names not known; wires that end beside it: dbus_out, clk, cont_peek[3], cont_peek[4], rset, 1'b0, 1'b0, a_dbus, acc_peek
  // register REG_B: pin names not known; wires that end beside it: dbus_out, dbus_out, clk, cont_peek[13], cont_peek[14], rset, 1'b0, 1'b0, b_dbus, REG_B_p10
  ROM #(.AddrBits(12), .Bits(32)) MCROM (.A({ir_peek, irc_peek}), .sel(1'b1), .D(cont_peek));
  Comparator #(.Bits(5)) comparator_1 (.a({irc_peek, cont_peek[7]}), .b(5'b00001), .eq(hlt));  // open: gt, lt
  // register REG_X: pin names not known; wires that end beside it: dbus_out, clk, cont_peek[2], cont_peek[6], rset, cont_peek[30], cont_peek[31], {ir_peek, irc_peek}, x_dbus, x_peek
  pc_controller PC_CONT (
    .PC_sel(cont_peek[20:18]), .bus_in(dbus_out), .flags_in(fr_peek), .clk(clk), .rset(rset),
    .cold_ena(1'b1), .pcli(PC_CONT_pcli), .pchi(PC_CONT_pchi), .pcl_bo(PC_CONT_pcl_bo),
    .pch_bo(PC_CONT_pch_bo));
  alu_v3 alu_v3_1 (
    .a_in(acc_peek), .b_in(REG_B_p10), .clk(clk), .OPSEL(cont_peek[17:15]), .rset(rset), .fi(cont_peek[21]),
    .fc(cont_peek[22]), .fo(cont_peek[23]), .bus_in(dbus_out), .x_in(x_peek), .a_din(cont_peek[3]),
    .x_din({cont_peek[31:30], cont_peek[2]}), .flags_peek(fr_peek), .flags_out(f_dbus), .alu_out(alu_dbus));
  // register PCH: pin names not known; wires that end beside it: PC_CONT_pch_bo, clk, PC_CONT_pchi, 1'b1, rset, PCH_p6, 1'b0, pca[15:8], pch_dbus
  // register PCL: pin names not known; wires that end beside it: PC_CONT_pcl_bo, clk, PC_CONT_pcli, 1'b1, rset, cont_peek[1], 1'b0, pca[7:0], pcl_dbus, PCH_p6
  // register MRH: pin names not known; wires that end beside it: dbus_out, clk, cont_peek[24], 1'b1, rset, MRH_p6, 1'b0, MRH_p8, MRH_p9, MRH_p9
  // register MRL: pin names not known; wires that end beside it: dbus_out, clk, cont_peek[5], 1'b1, rset, cont_peek[0], 1'b0, MRL_p8, MRL_p9, MRH_p6, MRL_p9
  mem_cont mem_cont_1 (
    .mrh(MRH_p8), .mrl(MRL_p8), .xreg(x_peek), .sp(SP_p9), .ms1(cont_peek[8]), .ms2(cont_peek[9]), .pca(pca),
    .abus(abus_out));
  // register SP: pin names not known; wires that end beside it: dbus_out, clk, 1'b0, cont_peek[29], rset, cont_peek[27], cont_peek[28], sp_dbus, SP_p9

  // Other names for the same wires on the sheet: abus[15:0] = abus_out; minc = cont_peek[0]; ci = cont_peek[1];
  //   xi = cont_peek[2]; ai = cont_peek[3]; ao = cont_peek[4]; mrli = cont_peek[5]; xo = cont_peek[6];
  //   end = cont_peek[7]; ms1 = cont_peek[8]; ms2 = cont_peek[9]; iri = cont_peek[10]; mo = cont_peek[11];
  //   mi = cont_peek[12]; bi = cont_peek[13]; bo = cont_peek[14]; als1 = cont_peek[15]; als2 = cont_peek[16];
  //   als3 = cont_peek[17]; pcc1 = cont_peek[18]; pcc2 = cont_peek[19]; pcc3 = cont_peek[20]; fi = cont_peek[21];
  //   fc = cont_peek[22]; fo = cont_peek[23]; mrhi = cont_peek[24]; pclo = cont_peek[25]; pcho = cont_peek[26];
  //   spu = cont_peek[27]; spd = cont_peek[28]; spo = cont_peek[29]; xu = cont_peek[30]; xd = cont_peek[31];
  //   dbus[7:0] = dbus_out; mo_dbus[7:0] = dbus_in

  // Notes on the sheet:
  //   contents of MCROM (hex, n*v repeats v):
  //   ff,88
endmodule
