// Digital circuit digital_sap1p.dig as structural Verilog
module digital_sap1p (
  input  clk,
  output [7:0] databus,
  output [7:0] out_3,
  output [7:0] out_4,
  output [15:0] addrbus,
  output [7:0] out_6,
  output [7:0] out_7,
  output [7:0] out_8,
  output out_9,
  output [11:0] out_10,
  output [31:0] out_11,
  output [7:0] out_12,
  output [7:0] out_13,
  output [7:0] out_14
);

  wire and_1_out, clk_t, decoder_2_out_0, decoder_2_out_2, decoder_2_out_3, Man_Auto_out, mrho, mrlo,
       not_1_out, or_1_out, PC_CONT_pchi, PC_CONT_pcli, PCL_cry, pco, rset, spd, spo, spu, t_ff_1_q,
       Tick_out, zpo;
  wire [3:0] mmio_1_p11, mmio_1_p12;
  wire [7:0] ALU_flags_peek, PC_CONT_pch_bo, PC_CONT_pcl_bo;

  T_FF t_ff_1 (.T(Man_Auto_out), .C(Man_Auto_out), .Q(t_ff_1_q), .nQ(out_9));
  Button Man_Auto (.out(Man_Auto_out));
  Button Tick (.out(Tick_out));
  and and_1 (and_1_out, t_ff_1_q, clk);
  not not_1 (not_1_out, out_11[0]);
  and and_2 (clk_t, or_1_out, not_1_out);
  Reset reset_1 ();  // open: out
  or or_1 (or_1_out, Tick_out, and_1_out);
  Button button_1 (.out(rset));
  LED led_1 (.in(databus[0]));
  register IR (
    .bus_in(databus), .clk(clk_t), .rfb(out_11[10]), .wtb(1'b0), .rset(rset), .inc(1'b0), .peek(out_10[11:4]));  // open: bus_out, cry
  Counter #(.Bits(4)) counter_1 (.en(1'b1), .C(clk_t), .clr(out_11[7]), .out(out_10[3:0]));  // open: ovf
  LED led_2 (.in(databus[2]));
  LED led_3 (.in(databus[4]));
  LED led_4 (.in(databus[1]));
  LED led_5 (.in(databus[3]));
  LED led_6 (.in(databus[6]));
  LED led_7 (.in(databus[5]));
  LED led_8 (.in(databus[7]));
  ROM #(.AddrBits(12), .Bits(32)) rom_1 (.A(out_10), .sel(1'b1), .D(out_11));
  register REG_A (
    .bus_in(databus), .clk(clk_t), .rfb(out_11[3]), .wtb(out_11[4]), .rset(rset), .inc(1'b0),
    .bus_out(databus), .peek(out_3));  // open: cry
  register REG_B (
    .bus_in(databus), .clk(clk_t), .rfb(out_11[13]), .wtb(out_11[14]), .rset(rset), .inc(1'b0),
    .bus_out(databus), .peek(out_4));  // open: cry
  LED led_9 (.in(out_11[0]));
  LED led_10 (.in(out_11[2]));
  LED led_11 (.in(out_11[1]));
  LED led_12 (.in(out_11[4]));
  LED led_13 (.in(out_11[6]));
  LED led_14 (.in(out_11[3]));
  LED led_15 (.in(out_11[5]));
  pc_controller PC_CONT (
    .PC_sel(out_11[20:18]), .bus_in(databus), .flags_in(ALU_flags_peek), .clk(clk_t), .rset(rset),
    .cold_ena(1'b1), .pcli(PC_CONT_pcli), .pchi(PC_CONT_pchi), .pcl_bo(PC_CONT_pcl_bo),
    .pch_bo(PC_CONT_pch_bo));
  LED led_16 (.in(out_11[8]));
  LED led_17 (.in(out_11[10]));
  LED led_18 (.in(out_11[7]));
  LED led_19 (.in(out_11[9]));
  LED led_20 (.in(ALU_flags_peek[0]));
  alu_v2 ALU (
    .a_in(out_3), .b_in(out_4), .clk(clk_t), .OPSEL(out_11[17:15]), .rset(rset), .fi(out_11[21]),
    .fc(out_11[22]), .fo(out_11[23]), .bus_in(databus), .flags_peek(ALU_flags_peek), .sub_peek(databus));  // open: bus_out
  register_sp register_sp_1 (
    .bus_in(databus), .clk(clk_t), .rfb(1'b0), .wtb(spo), .rset(rset), .inc(spu), .dec(spd),
    .bus_out(databus), .peek(out_14));  // open: cry
  LED led_21 (.in(out_11[12]));
  LED led_22 (.in(out_11[14]));
  LED led_23 (.in(out_11[11]));
  LED led_24 (.in(out_11[13]));
  LED led_25 (.in(ALU_flags_peek[2]));
  LED led_26 (.in(ALU_flags_peek[4]));
  LED led_27 (.in(ALU_flags_peek[1]));
  LED led_28 (.in(ALU_flags_peek[3]));
  LED led_29 (.in(out_11[18]));
  LED led_30 (.in(out_11[16]));
  LED led_31 (.in(out_11[15]));
  LED led_32 (.in(out_11[17]));
  register PCH (
    .bus_in(PC_CONT_pch_bo), .clk(clk_t), .rfb(PC_CONT_pchi), .wtb(pco), .rset(rset), .inc(PCL_cry),
    .bus_out(addrbus[15:8]));  // open: peek, cry
  register PCL (
    .bus_in(PC_CONT_pcl_bo), .clk(clk_t), .rfb(PC_CONT_pcli), .wtb(pco), .rset(rset), .inc(out_11[1]),
    .bus_out(addrbus[7:0]), .peek(out_6), .cry(PCL_cry));
  LED led_33 (.in(ALU_flags_peek[6]));
  LED led_34 (.in(ALU_flags_peek[5]));
  LED led_35 (.in(ALU_flags_peek[7]));
  LED led_36 (.in(out_11[20]));
  LED led_37 (.in(out_11[22]));
  LED led_38 (.in(out_11[19]));
  LED led_39 (.in(out_11[21]));
  register MRH (
    .bus_in(databus), .clk(clk_t), .rfb(out_11[24]), .wtb(mrho), .rset(rset), .inc(1'b0),
    .bus_out(addrbus[15:8]), .peek(out_7));  // open: cry
  register MRL (
    .bus_in(databus), .clk(clk_t), .rfb(out_11[5]), .wtb(mrlo), .rset(rset), .inc(1'b0),
    .bus_out(addrbus[7:0]), .peek(out_8));  // open: cry
  Decoder #(.Selector_Bits(2)) decoder_1 (.sel(out_11[9:8]), .out_0(pco), .out_1(mrho), .out_2(zpo), .out_3(spo));
  LED led_40 (.in(out_11[24]));
  LED led_41 (.in(out_11[23]));
  LED led_42 (.in(spd));
  LED led_43 (.in(spu));
  LED led_44 (.in(spo));
  assign addrbus[15:8] = zpo ? 8'h1 : 8'bz;  // Driver driver_1
  Driver #(.Bits(8)) driver_2 (.in({8{1'b0}}), .en(spo));  // open: out
  or or_2 (mrlo, mrho, zpo, spo);
  Decoder #(.Selector_Bits(2)) decoder_2 (
    .sel(addrbus[7:6]), .out_0(decoder_2_out_0), .out_2(decoder_2_out_2), .out_3(decoder_2_out_3));  // open: out_1
  RAMDualPort #(.AddrBits(6), .Bits(8)) ramdualport_1 (
    .A(addrbus[5:0]), .Din(databus), .str(out_11[12]), .C(clk_t), .ld(decoder_2_out_0), .D(out_12));
  // mmio mmio_1: pin names not known; wires that end beside it: addrbus[5:0], addrbus[5:0], databus, out_11[12], clk_t, decoder_2_out_2, rset, addrbus[5:0], {6{1'b0}}, out_12, mmio_1_p11, mmio_1_p12
  ROM #(.AddrBits(6), .Bits(8)) rom_2 (.A(addrbus[5:0]), .sel(decoder_2_out_3), .D(out_12));
  assign databus = out_11[11] ? out_12 : 8'bz;  // Driver driver_3
  Seven_Seg_Hex seven_seg_hex_1 (.d(mmio_1_p11), .dp(1'b0));
  Seven_Seg_Hex seven_seg_hex_2 (.d(mmio_1_p12), .dp(1'b0));

  assign out_13 = out_10[11:4];

  // Other names for the same wires on the sheet: abus[15:0] = addrbus; dbus[7:0] = databus; hlt = out_11[0];
  //   ci = out_11[1]; pcli = out_11[2]; ai = out_11[3]; ao = out_11[4]; mrli = out_11[5]; aluo = out_11[6];
  //   end = out_11[7]; ms1 = out_11[8]; ms2 = out_11[9]; iri = out_11[10]; mo = out_11[11]; mi = out_11[12];
  //   bi = out_11[13]; bo = out_11[14]; als1 = out_11[15]; als2 = out_11[16]; als3 = out_11[17]; pcc1 = out_11[18];
  //   pcc2 = out_11[19]; pcc3 = out_11[20]; fi = out_11[21]; fc = out_11[22]; fo = out_11[23]; mrhi = out_11[24]

  // Notes on the sheet:
  //   clk: Hz: 50
  //   addrbus: The Address Bus
  //   contents of rom_1 (hex, n*v repeats v):
  //   ff,88
  //   0-63 RAM
  //   128-191 IO
  //   192-255 ROM
  //   contents of rom_2 (hex, n*v repeats v):
  //   127*0,10
endmodule
