// Digital circuit example_16bit_registers.dig as structural Verilog
module example_16bit_registers (
  input  clk,
  input  [1:0] in_4,
  output [1:0] out_2,
  output [1:0] out_3
);

  wire button_1_out, button_2_out, counterpreset_2_ovf;

  Button button_1 (.out(button_1_out));
  Button button_2 (.out(button_2_out));
  CounterPreset #(.Bits(2)) counterpreset_1 (
    .en(counterpreset_2_ovf), .C(clk), .dir(1'b0), .in(2'b00), .ld(1'b0), .clr(1'b0), .out(out_3));  // open: ovf
  CounterPreset #(.Bits(2)) counterpreset_2 (
    .en(button_1_out), .C(clk), .dir(1'b0), .in(in_4), .ld(button_2_out), .clr(1'b0), .out(out_2),
    .ovf(counterpreset_2_ovf));
endmodule
