// Digital circuit gr8bit_main.dig as structural Verilog
module gr8bit_main (
  input  clk,
  output [7:0] databus,
  output [7:0] out_3,
  output [7:0] out_4,
  output [15:0] addrbus,
  output [7:0] out_6,
  output [7:0] out_7,
  output out_8,
  output [11:0] out_9,
  output [31:0] out_10,
  output [7:0] out_11,
  output [7:0] out_12,
  output [7:0] out_13,
  output [7:0] out_14,
  output [7:0] out_15
);

  wire and_1_out, and_3_out, and_4_out, clk_t, decoder_1_out_0, decoder_1_out_1, decoder_1_out_2,
       decoder_1_out_3, hlt, Man_Auto_out, MRL_cry, not_1_out, or_1_out, PC_CONT_pchi, PC_CONT_pcli, PCL_cry,
       pco, rset, t_ff_1_q, Tick_out;
  wire [7:0] ALU_flags_peek, IO_sd, MRH_bus_out, MRL_bus_out, PC_CONT_pch_bo, PC_CONT_pcl_bo, System_ROM_d;

  T_FF t_ff_1 (.T(Man_Auto_out), .C(Man_Auto_out), .Q(t_ff_1_q), .nQ(out_8));
  Button Man_Auto (.out(Man_Auto_out));
  Reset reset_1 ();  // open: out
  LED led_1 (.in(databus[0]));
  LED led_2 (.in(databus[1]));
  register IR (
    .bus_in(databus), .clk(clk_t), .rfb(out_10[10]), .wtb(1'b0), .rset(rset), .inc(1'b0), .peek(out_9[11:4]));  // open: bus_out, cry
  Counter #(.Bits(4)) irc (.en(1'b1), .C(clk_t), .clr(out_10[7]), .out(out_9[3:0]));  // open: ovf
  Button Tick (.out(Tick_out));
  and and_1 (and_1_out, t_ff_1_q, clk);
  not not_1 (not_1_out, hlt);
  Button button_1 (.out(rset));
  LED led_3 (.in(databus[2]));
  LED led_4 (.in(databus[4]));
  LED led_5 (.in(databus[3]));
  LED led_6 (.in(databus[5]));
  and and_2 (clk_t, or_1_out, not_1_out);
  LED led_7 (.in(databus[6]));
  LED led_8 (.in(databus[7]));
  register REG_B (
    .bus_in(databus), .clk(clk_t), .rfb(out_10[13]), .wtb(out_10[14]), .rset(rset), .inc(1'b0),
    .bus_out(databus), .peek(out_4));  // open: cry
  ROM #(.AddrBits(12), .Bits(32)) rom_1 (.A(out_9), .sel(1'b1), .D(out_10));
  Comparator #(.Bits(5)) comparator_1 (.a({out_9[3:0], out_10[7]}), .b(5'b00001), .eq(hlt));  // open: gt, lt
  or or_1 (or_1_out, Tick_out, and_1_out);
  register REG_A (
    .bus_in(databus), .clk(clk_t), .rfb(out_10[3]), .wtb(out_10[4]), .rset(rset), .inc(1'b0),
    .bus_out(databus), .peek(out_3));  // open: cry
  register_sp REG_X (
    .bus_in(databus), .clk(clk_t), .rfb(out_10[2]), .wtb(out_10[6]), .rset(rset), .inc(out_10[30]),
    .dec(out_10[31]), .bus_out(databus), .peek(out_13));  // open: cry
  LED led_9 (.in(out_10[0]));
  LED led_10 (.in(out_10[2]));
  LED led_11 (.in(out_10[1]));
  LED led_12 (.in(out_10[3]));
  LED led_13 (.in(out_10[4]));
  LED led_14 (.in(out_10[6]));
  LED led_15 (.in(out_10[5]));
  LED led_16 (.in(out_10[7]));
  pc_controller PC_CONT (
    .PC_sel(out_10[20:18]), .bus_in(databus), .flags_in(ALU_flags_peek), .clk(clk_t), .rset(rset),
    .cold_ena(1'b1), .pcli(PC_CONT_pcli), .pchi(PC_CONT_pchi), .pcl_bo(PC_CONT_pcl_bo),
    .pch_bo(PC_CONT_pch_bo));
  LED led_17 (.in(out_10[8]));
  LED led_18 (.in(out_10[10]));
  LED led_19 (.in(out_10[9]));
  LED led_20 (.in(out_10[11]));
  Seven_Seg_Hex seven_seg_hex_1 (.d(out_9[11:8]), .dp(1'b0));
  LED led_21 (.in(ALU_flags_peek[0]));
  LED led_22 (.in(ALU_flags_peek[1]));
  alu_v2 ALU (
    .a_in(out_3), .b_in(out_4), .clk(clk_t), .OPSEL(out_10[17:15]), .rset(rset), .fi(out_10[21]),
    .fc(out_10[22]), .fo(out_10[23]), .bus_in(databus), .x_in(out_13), .a_d(out_10[3]),
    .x_d({out_10[31], {2{out_10[2]}}}), .flags_peek(ALU_flags_peek), .bus_out(databus));
  LED led_23 (.in(out_10[12]));
  LED led_24 (.in(out_10[14]));
  LED led_25 (.in(out_10[13]));
  LED led_26 (.in(out_10[15]));
  Seven_Seg_Hex seven_seg_hex_2 (.d(out_9[7:4]), .dp(1'b1));
  LED led_27 (.in(ALU_flags_peek[2]));
  LED led_28 (.in(ALU_flags_peek[4]));
  LED led_29 (.in(ALU_flags_peek[3]));
  LED led_30 (.in(ALU_flags_peek[5]));
  LED led_31 (.in(out_10[18]));
  LED led_32 (.in(out_10[16]));
  LED led_33 (.in(out_10[19]));
  LED led_34 (.in(out_10[17]));
  Seven_Seg_Hex seven_seg_hex_3 (.d(out_9[3:0]), .dp(1'b0));
  register PCH (
    .bus_in(PC_CONT_pch_bo), .clk(clk_t), .rfb(PC_CONT_pchi), .wtb(pco), .rset(rset), .inc(PCL_cry),
    .bus_out(addrbus[15:8]), .peek(out_14));  // open: cry
  register PCL (
    .bus_in(PC_CONT_pcl_bo), .clk(clk_t), .rfb(PC_CONT_pcli), .wtb(pco), .rset(rset), .inc(out_10[1]),
    .bus_out(addrbus[7:0]), .peek(out_15), .cry(PCL_cry));
  LED led_35 (.in(ALU_flags_peek[6]));
  LED led_36 (.in(ALU_flags_peek[7]));
  LED led_37 (.in(out_10[20]));
  LED led_38 (.in(out_10[22]));
  LED led_39 (.in(out_10[21]));
  LED led_40 (.in(out_10[23]));
  register MRH (
    .bus_in(databus), .clk(clk_t), .rfb(out_10[24]), .wtb(1'b1), .rset(rset), .inc(MRL_cry),
    .bus_out(MRH_bus_out), .peek(out_6));  // open: cry
  register MRL (
    .bus_in(databus), .clk(clk_t), .rfb(out_10[5]), .wtb(1'b1), .rset(rset), .inc(out_10[0]),
    .bus_out(MRL_bus_out), .peek(out_7), .cry(MRL_cry));
  LED led_41 (.in(out_10[24]));
  LED led_42 (.in(out_10[26]));
  LED led_43 (.in(out_10[27]));
  LED led_44 (.in(out_10[25]));
  assign databus = out_10[26] ? out_14 : 8'bz;  // Driver driver_1
  assign databus = out_10[25] ? out_15 : 8'bz;  // Driver driver_2
  LED led_45 (.in(out_10[28]));
  LED led_46 (.in(out_10[30]));
  LED led_47 (.in(out_10[29]));
  LED led_48 (.in(out_10[31]));
  mem_cont mem_cont_1 (
    .mrh(MRH_bus_out), .mrl(MRL_bus_out), .xreg(out_13), .sp(out_12), .ms1(out_10[8]), .ms2(out_10[9]),
    .abus(addrbus), .pco(pco));
  register_sp SP (
    .bus_in(databus), .clk(clk_t), .rfb(1'b0), .wtb(out_10[29]), .rset(rset), .inc(out_10[27]),
    .dec(out_10[28]), .bus_out(databus), .peek(out_12));  // open: cry
  Decoder #(.Selector_Bits(2)) decoder_1 (
    .sel(addrbus[15:14]), .out_0(decoder_1_out_0), .out_1(decoder_1_out_1), .out_2(decoder_1_out_2),
    .out_3(decoder_1_out_3));
  assign databus = out_10[11] ? System_ROM_d : 8'bz;  // Driver driver_3
  and and_3 (and_3_out, out_10[12], decoder_1_out_0);
  and and_4 (and_4_out, decoder_1_out_2, out_10[12]);
  ROM #(.AddrBits(14), .Bits(8)) System_ROM (.A(addrbus[13:0]), .sel(decoder_1_out_3), .D(System_ROM_d));
  RAMDualPort #(.AddrBits(14), .Bits(8)) lowermem (
    .A(addrbus[13:0]), .Din(databus), .str(and_3_out), .C(clk_t), .ld(decoder_1_out_0), .D(System_ROM_d));
  mmio_v2 IO (
    .bus_in(databus), .rfb(and_4_out), .clk(clk_t), .wtb(decoder_1_out_2), .rset(rset),
    .addr_in(addrbus[5:0]), .addr_set({6{1'b0}}), .bus_out(System_ROM_d), .sd(IO_sd));
  LED led_49 (.in(IO_sd[0]));
  LED led_50 (.in(IO_sd[2]));
  LED led_51 (.in(IO_sd[1]));
  LED led_52 (.in(IO_sd[3]));
  Seven_Seg_Hex seven_seg_hex_4 (.d(IO_sd[7:4]), .dp(1'b0));
  LED led_53 (.in(IO_sd[4]));
  LED led_54 (.in(IO_sd[6]));
  LED led_55 (.in(IO_sd[5]));
  LED led_56 (.in(IO_sd[7]));
  Seven_Seg_Hex seven_seg_hex_5 (.d(IO_sd[3:0]), .dp(1'b0));

  assign out_11 = out_9[11:4];

  // Other names for the same wires on the sheet: abus[15:0] = addrbus; dbus[7:0] = databus;
  //   ir_peek[7:0] = out_9[11:4]; irc_peek[3:0] = out_9[3:0]; minc = out_10[0]; ci = out_10[1]; xi = out_10[2];
  //   ai = out_10[3]; ao = out_10[4]; mrli = out_10[5]; xo = out_10[6]; end = out_10[7]; ms1 = out_10[8];
  //   ms2 = out_10[9]; iri = out_10[10]; mo = out_10[11]; mi = out_10[12]; bi = out_10[13]; bo = out_10[14];
  //   als1 = out_10[15]; als2 = out_10[16]; als3 = out_10[17]; pcc1 = out_10[18]; pcc2 = out_10[19];
  //   pcc3 = out_10[20]; fi = out_10[21]; fc = out_10[22]; fo = out_10[23]; mrhi = out_10[24]; pclo = out_10[25];
  //   pcho = out_10[26]; spu = out_10[27]; spd = out_10[28]; spo = out_10[29]; xu = out_10[30]; xd = out_10[31];
  //   x_peek[7:0] = out_13

  // Notes on the sheet:
  //   clk: Hz: 200
  //   addrbus: The Address Bus
  //   contents of rom_1 (hex, n*v repeats v):
  //   ff,88
  //   Bank Sel
  //   Future Video Memory
  //   0x4000-0x7FFF
  //   IO Space 0x8000 - 0xBFFF
  //   contents of System_ROM (hex, n*v repeats v):
  //   127*0,10
  //   ROM 0xC000 - 0xFFFF
endmodule
