// Digital circuit mmio.dig as structural Verilog
module mmio (
  input  [7:0] bus_in,
  input  rfb,
  input  clk,
  input  wtb,
  input  rset,
  input  [5:0] addr_in,
  input  [5:0] addr_set,
  output [7:0] bus_out,
  output [3:0] dout_hi,
  output [3:0] dout_low
);

  wire and_1_out, and_2_out, comparator_1_eq;

  Comparator #(.Bits(6)) comparator_1 (.a(addr_in), .b(addr_set), .eq(comparator_1_eq));  // open: gt, lt
  and and_1 (and_1_out, rfb, comparator_1_eq);
  and and_2 (and_2_out, wtb, comparator_1_eq);
  register register_1 (
    .bus_in(bus_in), .clk(clk), .rfb(and_1_out), .wtb(and_2_out), .rset(rset), .inc(1'b0), .bus_out(bus_out),
    .peek({dout_hi, dout_low}));  // open: cry
  // Pins of 1 and 4 bits meet at dout_low
  // Pins of 1 and 4 bits meet at dout_hi
endmodule
