// Digital circuit old_cold.dig as structural Verilog
module old_cold (
  input  clk,
  input  in_3,
  input  [7:0] in_4,
  output out_2,
  output [7:0] out_5,
  output out_6
);

  wire and_1_out, clk_t, coldstart_2_q, coldstart_3_nq, coldstart_nq, Man_Auto_out, rs_ff_as_1_q, rset,
       t_ff_1_q, Tick_out;
  wire [7:0] driver_1_out;
  wire [8:0] driverinvsel_3_out;
  wire [8:8] driverinvsel_1_out;

  Monoflop #(.timerDelay(2)) coldstart (.C(clk_t), .R(rset), .nQ(coldstart_nq));  // open: Q
  assign driverinvsel_1_out[8] = ~coldstart_nq ? in_3 : 1'bz;  // DriverInvSel driverinvsel_1
  assign {driverinvsel_1_out[8], driver_1_out} = coldstart_nq ? 9'h1fc : 9'bz;  // Driver driver_1
  assign driver_1_out = ~coldstart_nq ? in_4 : 8'bz;  // DriverInvSel driverinvsel_2
  Button Man_Auto (.out(Man_Auto_out));
  T_FF t_ff_1 (.T(Man_Auto_out), .C(Man_Auto_out), .Q(t_ff_1_q), .nQ(out_2));
  Button Tick (.out(Tick_out));
  and and_1 (and_1_out, t_ff_1_q, clk);
  RS_FF_AS rs_ff_as_1 (.S(clk_t), .R(rset), .Q(rs_ff_as_1_q));  // open: nQ
  or or_1 (clk_t, Tick_out, and_1_out);
  Monoflop coldstart_2 (.C(rs_ff_as_1_q), .R(1'b0), .Q(coldstart_2_q));  // open: nQ
  Reset reset_1 ();  // open: out
  Button button_1 (.out(rset));
  assign driverinvsel_3_out[7:0] = ~coldstart_2_q ? in_4 : 8'bz;  // DriverInvSel driverinvsel_3
  DriverInvSel driverinvsel_4 (.en(coldstart_2_q), .out(driverinvsel_3_out[8]));  // open: in
  Driver #(.Bits(9)) driver_2 (.en(coldstart_2_q), .out(driverinvsel_3_out));  // open: in
  Monoflop #(.timerDelay(2)) coldstart_3 (.C(clk_t), .R(rset), .nQ(coldstart_3_nq));  // open: Q
  DriverInvSel driverinvsel_5 (.en(coldstart_3_nq), .out(out_6));  // open: in
  Driver #(.Bits(9)) driver_3 (.en(coldstart_3_nq), .out({out_6, out_5}));  // open: in
  assign out_5 = ~coldstart_3_nq ? in_4 : 8'bz;  // DriverInvSel driverinvsel_6

  // Other names for the same wires on the sheet: dbus[7:0] = in_4; pcli = in_3

  // Notes on the sheet:
  //   old coldstart
endmodule
