// Digital circuit pc.dig as structural Verilog
module pc (
  input  abus_in,
  input  dbus_in,
  input  jmp,
  input  incr,
  input  ena
);

  CounterPreset #(.Bits(6), .isProgramCounter("true")) pri (.dir(1'b0));  // open: en, C, in, ld, clr, out, ovf
  CounterPreset #(.Bits(6), .isProgramCounter("true")) bank (.dir(1'b0));  // open: en, C, in, ld, clr, out, ovf
endmodule
