// Digital circuit pc_controller.dig as structural Verilog
module pc_controller (
  input  [2:0] PC_sel,
  input  [7:0] bus_in,
  input  [7:0] flags_in,
  input  clk,
  input  rset,
  input  cold_ena,
  output pcli,
  output pchi,
  output [7:0] pcl_bo,
  output [7:0] pch_bo
);

  wire and_1_out, and_2_out, and_3_out, and_4_out, and_5_out, and_6_out, and_7_out, and_8_out, and_9_out,
       bitselector_1_out, bitselector_2_out, coldstart_q, decoder_1_out_1, decoder_1_out_2, decoder_1_out_3,
       not_1_out, rs_ff_as_1_q;

  RS_FF_AS rs_ff_as_1 (.S(clk), .R(rset), .Q(rs_ff_as_1_q));  // open: nQ
  not not_1 (not_1_out, PC_sel[2]);
  BitSelector #(.Selector_Bits(3)) bitselector_1 (.in(flags_in), .sel(3'b001), .out(bitselector_1_out));
  BitSelector #(.Selector_Bits(3)) bitselector_2 (.in(flags_in), .sel(3'b000), .out(bitselector_2_out));
  Decoder #(.Selector_Bits(2)) decoder_1 (
    .sel(PC_sel[1:0]), .out_1(decoder_1_out_1), .out_2(decoder_1_out_2), .out_3(decoder_1_out_3));  // open: out_0
  Monoflop #(.timerDelay(2)) coldstart (.C(rs_ff_as_1_q), .R(rset), .Q(coldstart_q));  // open: nQ
  and and_1 (and_1_out, decoder_1_out_2, bitselector_1_out);
  and and_2 (and_2_out, decoder_1_out_3, bitselector_2_out);
  and and_3 (and_3_out, cold_ena, coldstart_q);
  assign pcl_bo = ~and_3_out ? bus_in : 8'bz;  // DriverInvSel driverinvsel_1
  and and_4 (and_4_out, decoder_1_out_1, not_1_out);
  and and_5 (and_5_out, decoder_1_out_1, PC_sel[2]);
  and and_6 (and_6_out, and_1_out, not_1_out);
  and and_7 (and_7_out, and_1_out, PC_sel[2]);
  and and_8 (and_8_out, and_2_out, not_1_out);
  and and_9 (and_9_out, and_2_out, PC_sel[2]);
  assign pch_bo = ~and_3_out ? bus_in : 8'bz;  // DriverInvSel driverinvsel_2
  assign pcl_bo = and_3_out ? 8'hfc : 8'bz;  // Driver driver_1
  assign pch_bo = and_3_out ? {8{1'b1}} : 8'bz;  // Driver driver_2
  assign pcli = and_3_out ? and_3_out : 1'bz;  // Driver driver_3
  assign pchi = and_3_out ? and_3_out : 1'bz;  // Driver driver_4
  assign pcli = and_4_out ? and_4_out : 1'bz;  // Driver driver_5
  assign pchi = and_5_out ? and_5_out : 1'bz;  // Driver driver_6
  assign pcli = and_6_out ? and_6_out : 1'bz;  // Driver driver_7
  assign pchi = and_7_out ? and_7_out : 1'bz;  // Driver driver_8
  assign pcli = and_8_out ? and_8_out : 1'bz;  // Driver driver_9
  assign pchi = and_9_out ? and_9_out : 1'bz;  // Driver driver_10
  PullDown pulldown_1 (.out(pcli));
  PullDown pulldown_2 (.out(pchi));

  // Notes on the sheet:
  //   Equal/Zero
  //   Carry
  //   PCUU = 0b000 << 18 # PC Counters Unselected
  //   PLLU = 0b001 << 18 # PC Low in from bus, unconditional
  //   PLHU = 0b101 << 18 # PC Hi  in from bus, unconditional
  //   PLLE = 0b010 << 18 # PC Low in from bus, On Equal
  //   PLHE = 0b110 << 18 # PC Hi  in from bus, On Equal
  //   PLLC = 0b011 << 18 # PC Low in from bus, On Carry
  //   PLHC = 0b111 << 18 # PC Hi  in from bus, On Carry
  //   ----
  //   NV1B DIZC
endmodule

/* Test case Coldstart:
clk rset cold_ena bus_in pcl_bo pch_bo pcli pchi
C   0    1        Z      0xFC   0xFF   1    1
C   0    1        Z      0xFC   0xFF   1    1
# C   0    1        Z      X      X      X    X
C   0    1        Z      X       X    0    0
C   0    1        Z      X       X    0    0
C   1    1        Z      X       X    0    0
C   0    1        Z      0xFC   0xFF   1    1
*/

/* Test case Test Jumps:
clk PC_sel flags_in pcli pchi bus_in pch_bo pcl_bo
# Not selected
C 0b000 0b00000000 0 0 X X X
# unconditional jump
C 0b001 0b00000000 1 0 X X X
C 0b101 0b00000000 0 1 X X X
# jump if equal
C 0b010 0b00000010 1 0 0x12 X X
C 0b110 0b00000010 0 1 0x12 X X
C 0b010 0b11111101 0 0 0x12 X X
C 0b110 0b11111101 0 0 0x12 X X
# jump if carry
C 0b011 0b00000001 1 0 X X X
C 0b111 0b00000001 0 1 X X X
C 0b111 0b11111110 0 0 X X X
*/
