// Digital circuit register.dig as structural Verilog
module register (
  input  [7:0] bus_in,
  input  clk,
  input  rfb,
  input  wtb,
  input  rset,
  input  inc,
  output [7:0] bus_out,
  output [7:0] peek,
  output cry
);

  wire [7:0] driver_1_out;

  assign driver_1_out = rfb ? bus_in : 8'bz;  // Driver driver_1
  CounterPreset #(.Bits(8)) counterpreset_1 (
    .en(inc), .C(clk), .dir(1'b0), .in(driver_1_out), .ld(rfb), .clr(rset), .out(peek), .ovf(cry));
  assign bus_out = wtb ? peek : 8'bz;  // Driver driver_2
endmodule

/* Test case test-bus-out:
clk wtb inc peek bus_out
1 1   0    00000000 00000000
0 0   0    00000000 Z
1 0   1    00000001 Z
0 0   0    00000001 Z
*/

/* Test case test-bus-in:
clk rfb bus_in peek
0 0 00000001 00000000
1 0 00000001 00000000
0 1 00000001 00000000
1 1 00000001 00000001
*/
