// Digital circuit register_sp.dig as structural Verilog
module register_sp (
  input  [7:0] bus_in,
  input  clk,
  input  rfb,
  input  wtb,
  input  rset,
  input  inc,
  input  dec,
  output [7:0] bus_out,
  output [7:0] peek,
  output cry
);

  wire or_1_out;
  wire [7:0] driver_1_out;

  assign driver_1_out = rfb ? bus_in : 8'bz;  // Driver driver_1
  or or_1 (or_1_out, dec, inc);
  CounterPreset #(.Bits(8)) counterpreset_1 (
    .en(or_1_out), .C(clk), .dir(dec), .in(driver_1_out), .ld(rfb), .clr(rset), .out(peek), .ovf(cry));
  assign bus_out = wtb ? peek : 8'bz;  // Driver driver_2
endmodule

/* Test case SP Tests:
clk inc dec rset peek
C   1   0   0 1
C   1   0   0 2
C   1   0   0 3
C   0   1   0 2
C   0   1   0 1
C   0   0   1 0
*/

/* Test case test-bus-out:
clk wtb inc dec rset peek bus_out
C 1   0 0 1  00000000 00000000
C 1   0 0 0  00000000 00000000
C 0   0 0 0 00000000 Z
C 0   1 0 0 00000001 Z
C 0   0 0 0 00000001 Z
*/

/* Test case test-bus-in:
clk rfb bus_in peek
0 0 00000001 00000000
1 0 00000001 00000000
0 1 00000001 00000000
1 1 00000001 00000001
*/
