// Digital circuit uart.dig as structural Verilog
module uart (
  input  clk,
  input  send,
  input  data_in,
  output [7:0] data_out,
  output char_av
);

  wire [15:8] keyboard_1_d;

  Terminal terminal_1 (.D(data_in), .C(clk), .en(send));
  Keyboard keyboard_1 (.C(clk), .en(1'b1), .D({keyboard_1_d, data_out}), .av(char_av));
endmodule
